// Logisim project alu.circ as structural Verilog: 1 circuit, main circuit alu
module alu (
  input  [31:0] A,
  input  [31:0] B,
  input  [3:0] ALUSel,
  output [31:0] Result
);

  wire adder_1_cout;
  wire [31:0] add0, sll0;

  Adder #(.width(32)) adder_1 (.a(A), .b(B), .out(add0), .cout(adder_1_cout));  // open: cin
  Shifter #(.width(32)) shifter_1 (.in(A), .\dist (B[4:0]), .out(sll0));

  // Notes on the sheet:
  //   INPUTS to your circuit
  //   DON'T CHANGE THE LOCATIONS OF THE INPUTS AND OUTPUTS!
  //   OUTPUT from your circuit
endmodule
